# Fritzing sketch CDS (saved by Fritzing 0.8.7b)
breadboards: 1

parts:
  부품1 = Arduino Uno (Rev3)
  R2 = Resistor [tolerance=±5% resistance=10k package=THT]
  R3 = Photocell (LDR) [package=THT]

nets:
  N1: 부품1.A0, R2.Pin_1, R3.pin_0
  N2: 부품1.GND, R2.Pin_0
  N3: 부품1.5V, R3.pin_1
