# Fritzing sketch SR04+LCD+dht (saved by Fritzing 0.8.7b)
breadboards: 1

parts:
  부품1 = LCD1602-I2C
  부품2 = Arduino Uno (Rev3)
  DHT11_2 = DHT11 module

nets:
  GND: 부품1.GND, 부품2.GND, DHT11_2.GND
  VCC: 부품1.VCC, 부품2.5V, DHT11_2.VCC
  N1: 부품1.SDA, 부품2.A4/SDA
  N2: 부품1.SCL, 부품2.A5/SCL
  N3: 부품2.D2, DHT11_2.DATA

custom parts:
  LCD1602-I2C: A standard character display, usually with 2x16 characters. Comes in many colors with LCM1602 IIC attached.
  DHT11 module: https://cdn-learn.adafruit.com/downloads/pdf/dht.pdf DHT11 black pcb module reference by:https://github.com/adafruit/Fritzing-Library/blob/master/parts/DHT11%20Humitidy%20and%20Temperature%20Sensor.fzpz
